# Fritzing sketch L298N - Arduino Uno (saved by Fritzing 0.9.3b)

parts:
  S1 = H-Bridge with L298N
  Componente1 = Arduino Uno (Rev3)
  M1 = DC Motor  # not connected
  M2 = DC Motor
  VCC1 = Battery block 12V

nets:
  N1: S1.12V, VCC1.+
  GND: S1.GND, Componente1.GND, VCC1.-
  5V: S1.5V, Componente1.VIN
  N2: S1.ENA, Componente1.D9_PWM
  N3: S1.IN1, Componente1.D8
  N4: S1.IN2, Componente1.D7
  N5: S1.IN3, Componente1.D13/SCK
  N6: S1.IN4, Componente1.D12/MISO
  N7: S1.ENB, Componente1.D11_PWM/MOSI
  N8: S1.M1-01, M2.pin_2

notes:
  12 v Battery
  Motor 1
  Motor 2

custom parts:
  H-Bridge with L298N: h-bridge
  Battery block 12V: Your standard 12 Volts battery block
